# Fritzing sketch breadboard_schema (saved by Fritzing 1.0.2b)
breadboards: 1

parts:
  Mod1 = Raspberry Pi Pico
  DHT11_1 = DHT11 module
  ZS-042_RTC1 = ZS-042 RTC Module  # not connected
  microSD1 = MicroSD Card Module  # not connected
  LED1 = smd LED [color="Red (633nm)" package="0805 [SMD]"]
  R1 = Resistor [tolerance=±5% resistance=220 package="1206 [SMD]"]
  S2 = Pushbutton [package="[THT]"]

nets:
  N1: Mod1.pin_1, Mod1.pin_39, DHT11_1.GND, LED1.cathode, S2.Pin_1, S2.Pin_2, S2.Pin_3, S2.Pin_4
  N2: Mod1.pin_3, Mod1.pin_8, Mod1.pin_13, Mod1.pin_18, Mod1.pin_23, Mod1.pin_28, Mod1.pin_33, Mod1.pin_38
  N3: Mod1.pin_7, DHT11_1.DATA
  N4: Mod1.pin_20, R1.Pin_0
  N5: Mod1.pin_37, DHT11_1.VCC
  N6: LED1.anode, R1.Pin_1

custom parts:
  Raspberry Pi Pico: Raspberry Pi Pico. Based around the RP2040 microcontroller the Pico is a low cost microcontroller device bringing Raspberry Pi quality, cost, and easy of use to the microcontroller space. Jan 2021, Split part in to two versions: tht (this one) and SMD. This one will drill holes for a .1 in header in pcb to allow plugging in the module as well as providing pads to solder the module to the top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
  DHT11 module: https://cdn-learn.adafruit.com/downloads/pdf/dht.pdf DHT11 black pcb module reference by:https://github.com/adafruit/Fritzing-Library/blob/master/parts/DHT11%20Humitidy%20and%20Temperature%20Sensor.fzpz
